# Fritzing sketch AnalogInput1 (saved by Fritzing 0.7.9b)
breadboards: 1

parts:
  Arduino2 = Arduino
  R1 = Rotary Potentiometer (Large) [maximum_resistance=100kΩ package=THT]

nets:
  GND: Arduino2.GND, R1.leg1
  5V: Arduino2.+5V, R1.leg2
  N1: Arduino2.A0, R1.wiper
