# Fritzing sketch AnalogInput2 (saved by Fritzing 0.7.9b)
breadboards: 1

parts:
  Arduino2 = Arduino
  R1 = Rotary Potentiometer (Large) [maximum_resistance=100kΩ package=THT]
  LED1 = LED - 5mm [color="Red (633nm)" package="5 mm [THT]"]
  R2 = Resistor [tolerance=±5% resistance=270 package=THT]

nets:
  GND: Arduino2.GND, R1.leg1, R2.Pin_0
  N1: Arduino2.D9, LED1.anode
  5V: Arduino2.+5V, R1.leg2
  N2: Arduino2.A0, R1.wiper
  N3: LED1.cathode, R2.Pin_1
