# Fritzing sketch Button+Pullup (saved by Fritzing 0.7.9b)
breadboards: 1

parts:
  LED1 = Red LED - 5mm
  Arduino1 = Arduino
  S1 = Pushbutton [package="[THT]"]
  R1 = Resistor [tolerance=±5% resistance=270 package=THT]
  R2 = Resistor [tolerance=±5% resistance=1k package=THT]

nets:
  GND: LED1.cathode, Arduino1.GND, S1.Pin_1, S1.Pin_2
  N1: LED1.anode, R1.Pin_0
  N2: Arduino1.D9, R1.Pin_1
  N3: Arduino1.D5, S1.Pin_3, S1.Pin_4, R2.Pin_0
  5V: Arduino1.+5V, R2.Pin_1
