# Fritzing sketch HBridge (saved by Fritzing 0.7.11b)
breadboards: 1

parts:
  IC1 = H-Bridge [package=THT]
  M1 = DC Motor
  Arduino1 = Arduino

nets:
  5V: IC1.1_2EN, IC1.VCC2, IC1.VCC1, Arduino1.+5V
  N1: IC1.1A, Arduino1.D10
  N2: IC1.1Y, M1.pin_1
  GND: IC1.GND2, IC1.GND3, Arduino1.GND
  N3: IC1.2Y, M1.pin_2
  N4: IC1.2A, Arduino1.D9

notes:
  This is not actually the part we used in class (L293D), but it has the same pin configuration. The part shown here (SN754410) would need additional diodes, which the L293D has built in.
