# Fritzing sketch Motor1 (saved by Fritzing 0.7.9b)
breadboards: 1

parts:
  M1 = DC Motor
  D1 = Rectifier Diode [part_number=1N4001 package="300 mil [THT]"]
  Arduino1 = Arduino
  Q1 = NPN-Transistor [package="TO92 [THT]"]

nets:
  N1: M1.pin_1, D1.anode, Q1.C
  5V: M1.pin_2, D1.cathode, Arduino1.+5V
  GND: Arduino1.GND, Q1.E
  N2: Arduino1.D11, Q1.B
