# Fritzing sketch Photoresistor2 (saved by Fritzing 0.7.9b)
breadboards: 1

parts:
  R1 = Photocell (LDR) [package=THT]
  R2 = Resistor [resistance=680k tolerance=±5% package=THT]
  LED1 = Red LED - 5mm [package="5 mm [THT]"]
  R3 = Resistor [resistance=330 tolerance=±5% package=THT]
  Arduino1 = Arduino

nets:
  5V: R1.pin_0, Arduino1.+5V
  N1: R1.pin_1, R2.Pin_0, Arduino1.A0
  GND: R2.Pin_1, R3.Pin_0, Arduino1.GND
  N2: LED1.cathode, R3.Pin_1
  N3: LED1.anode, Arduino1.D9
