# Fritzing sketch RGB_LED1 (saved by Fritzing 0.7.9b)
breadboards: 1

parts:
  Arduino1 = Arduino
  LED1 = RGB LED (com. anode, rbg) [package="5 mm [THT]"]
  R4 = Resistor [tolerance=±5% resistance=220 package=THT]
  R5 = Resistor [tolerance=±5% resistance=220 package=THT]
  R6 = Resistor [tolerance=±5% resistance=220 package=THT]

nets:
  GND: Arduino1.GND
  N1: Arduino1.D11, R4.Pin_1
  N2: Arduino1.D10, R5.Pin_1
  N3: Arduino1.D9, R6.Pin_1
  5V: Arduino1.+5V, LED1.common_anode
  N4: LED1.red_cathode, R4.Pin_0
  N5: LED1.blue_cathode, R6.Pin_0
  N6: LED1.green_cathode, R5.Pin_0
