# Fritzing sketch RGB_LED2 (saved by Fritzing 0.7.9b)
breadboards: 1

parts:
  Arduino1 = Arduino
  LED1 = RGB LED (com. anode, rbg) [package="5 mm [THT]"]
  R4 = Resistor [tolerance=±5% resistance=220 package=THT]
  R5 = Resistor [tolerance=±5% resistance=220 package=THT]
  R6 = Resistor [tolerance=±5% resistance=220 package=THT]
  R7 = Rotary Potentiometer (Large) [maximum_resistance=10kΩ package=THT]
  R8 = Rotary Potentiometer (Large) [maximum_resistance=10kΩ package=THT]
  R9 = Rotary Potentiometer (Large) [maximum_resistance=10kΩ package=THT]

nets:
  GND: Arduino1.GND, R7.leg2, R8.leg2, R9.leg2
  N1: Arduino1.D11, R4.Pin_1
  N2: Arduino1.D10, R5.Pin_1
  N3: Arduino1.D9, R6.Pin_1
  5V: Arduino1.+5V, LED1.common_anode, R7.leg1, R8.leg1, R9.leg1
  N4: Arduino1.A0, R9.wiper
  N5: Arduino1.A1, R7.wiper
  N6: Arduino1.A2, R8.wiper
  N7: LED1.red_cathode, R4.Pin_0
  N8: LED1.blue_cathode, R6.Pin_0
  N9: LED1.green_cathode, R5.Pin_0
