# Fritzing sketch Servo (saved by Fritzing 0.7.9b)
breadboards: 1

parts:
  J1 = Basic Servo
  Arduino1 = Arduino
  S1 = Pushbutton [package="[THT]"]
  S2 = Pushbutton [package="[THT]"]
  S3 = Pushbutton [package="[THT]"]
  S4 = Pushbutton [package="[THT]"]

nets:
  GND: J1.gnd, Arduino1.GND, S1.Pin_1, S1.Pin_2, S2.Pin_1, S2.Pin_2, S3.Pin_1, S3.Pin_2, S4.Pin_1, S4.Pin_2
  5V: J1.vcc, Arduino1.+5V
  N1: J1.pulse, Arduino1.D11
  N2: Arduino1.D5, S4.Pin_3, S4.Pin_4
  N3: Arduino1.D4, S3.Pin_3, S3.Pin_4
  N4: Arduino1.D3, S2.Pin_3, S2.Pin_4
  N5: Arduino1.D2, S1.Pin_3, S1.Pin_4
