# Fritzing sketch Christmas_Lights (saved by Fritzing 0.8.3b)
breadboards: 1

parts:
  Arduino1 = Arduino
  IC1 = H-Bridge [package=THT]
  IC2 = H-Bridge [package=THT]
  LED1 = RGB LED - (4 legs) [package="5 mm [THT]"]

nets:
  GND: Arduino1.GND, IC1.GND2, IC1.GND4, IC2.GND2, IC2.GND4, LED1.common_anode
  N1: Arduino1.D11, IC2.1A
  N2: Arduino1.D10, IC1.4A
  N3: Arduino1.D9, IC1.1A
  5V: Arduino1.+5V, IC1.1_2EN, IC1.3_4EN, IC1.VCC1, IC2.1_2EN, IC2.3_4EN, IC2.VCC1
  N4: Arduino1.VIN, IC1.VCC2, IC2.VCC2
  N5: IC1.1Y, LED1.red_cathode
  N6: IC1.4Y, LED1.blue_cathode
  N7: IC2.1Y, LED1.green_cathode

notes:
  Fun with Arduino by Rob Purser is licensed under a
  Creative Commons
  Attribution-NonCommercial-ShareAlike 3.0 Unported License.
  Based on a work at https://sites.google.com/site/funarduino/
  Copyright 2013, Rob Purser
  We want to power the LEDs directly from the batteries, not from the +5V on the Arduino
